# Fritzing sketch diffbot (saved by Fritzing 0.9.6b)
breadboards: 1

parts:
  RPLidarA2M2 = RPLidar A2 M8 Serial to USB converter
  RPLidarA2M3 = RPLidar A2 M8
  IC1 = Grove - I2C Motor Driver V1.3 [package="DIP (Dual Inline) [THT]"]
  USBTTL1 = Micro USB B Plug
  USBTTL2 = USB A Plug
  DG01D-E_Motor_with_Encoder1 = Hobby Motor with Encoder - Metal Gear (DG01D-E) [part_number=VT-E-G25A-06-177E]
  DG01D-E_Motor_with_Encoder2 = Hobby Motor with Encoder - Metal Gear (DG01D-E) [part_number=VT-E-G25A-06-177E]
  Teensy1 = Teensy 4.0
  VCC1 = 4 x AAA Battery Mount
  Mod1 = Raspberry Pi 4B
  USBTTL3 = USB A Plug
  USBTTL4 = Micro USB B Plug

nets:
  N1: RPLidarA2M2.RX, RPLidarA2M3.RX
  N2: RPLidarA2M2.TX, RPLidarA2M3.TX
  GND: RPLidarA2M2.GND, RPLidarA2M3.GND
  N3: RPLidarA2M2.PWM, RPLidarA2M3.PWM
  5V: RPLidarA2M2.5V, RPLidarA2M3.VCC
  N4: IC1.M1-, DG01D-E_Motor_with_Encoder1.M-
  N5: IC1.M1+, DG01D-E_Motor_with_Encoder1.M+
  N6: IC1.M2-, DG01D-E_Motor_with_Encoder2.M-
  N7: IC1.M2+, DG01D-E_Motor_with_Encoder2.M+
  N8: IC1.GND, VCC1.-
  N9: IC1.VS, VCC1.+
  N10: USBTTL1.usb, USBTTL2.usb
  N11: DG01D-E_Motor_with_Encoder1.V, DG01D-E_Motor_with_Encoder2.V, Mod1.3V3
  N12: DG01D-E_Motor_with_Encoder1.H2, Teensy1.pin_8
  N13: DG01D-E_Motor_with_Encoder1.H1, Teensy1.pin_7
  GND_2: DG01D-E_Motor_with_Encoder1.Gnd, DG01D-E_Motor_with_Encoder2.Gnd
  N14: DG01D-E_Motor_with_Encoder2.H2, Teensy1.pin_10
  N15: DG01D-E_Motor_with_Encoder2.H1, Teensy1.pin_9
  N16: Teensy1.pin_1, Teensy1.pin_32
  N17: USBTTL3.usb, USBTTL4.usb

notes:
  - G (Blue): hall power negative
  - H1 (Green): hall H1 output signal, square wave
  - H2 (Yellow): hall H2 output signal, square wave
  - V (Orange): hall power positive
  - M+ (Red): motor positive pole
  - M- (Brown): motor negative pole

custom parts:
  RPLidar A2 M8 Serial to USB converter: SLAMTEC RPLidar A2 M8 Serial to USB converter
  RPLidar A2 M8: SLAMTEC RPLidar A2 M8
  Grove - I2C Motor Driver V1.3: The Grove - I2C Motor Driver V1.3 (latest version) can directly control Stepper Motor or DC Motor. Its heart is a dual channel H-bridge driver chip（L298N）that can handle current up to 2A per channel, controlled by an Atmel ATmega8L which handles the I2C communication with platforms such as Arduino. Both motors can be driven simultaneously while set to a different speed and direction. It can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
  Micro USB B Plug: Micro USB B Plug breadboard only for documetnation purposes.
  USB A Plug: USB A Plug breadboard only for documetnation purposes.
  Hobby Motor with Encoder - Metal Gear (DG01D-E): The DG01D-E is a single hobby motor with a hall speed encoder. This motor requires a voltage between 3-9V, has a gearbox ratio of 1:48 and a speed of 90RPM at 4.5V. The voltage between positive and negative is determined according to the power supply voltage of the single chip microcomputer used, generally 3.3V or 5V is used. The hall sensor can sense the North and South poles of its magnetic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
  Teensy 4.0: The Teensy is a complete USB-based microcontoller development system, in a very small footprint, capable of implementing many types of projects. All programming is done via the USB port. No special programmer is needed, only a standard micro-USB cable and a PC or Macintosh with a USB port.
