# Fritzing sketch remo-side (saved by Fritzing 0.9.4)
breadboards: 1

parts:
  Teensy1 = Teensy 4.0
  Mod2 = Grove I2C hub
  DG01D-E_Motor_with_Encoder3 = Hobby Motor with Encoder - Metal Gear (DG01D-E) [part_number=VT-E-G25A-06-177E]
  DG01D-E_Motor_with_Encoder4 = Hobby Motor with Encoder - Metal Gear (DG01D-E) [part_number=VT-E-G25A-06-177E]
  RPLidarA2M4 = RPLidar A2 M8 Serial to USB converter
  USBTTL5 = Micro USB B Plug
  USBTTL6 = USB A Plug
  USBTTL7 = Micro USB B Plug
  USBTTL8 = USB A Plug
  Mod3 = Raspberry Pi 4B
  RPLidarA2M5 = RPLidar A2 M8
  Part1 = Adafruit DC+Stepper FeatherWing [part_number="Adafruit #2927"]
  VCC2 = 4 x AAA Battery Mount
  USBTTL9 = Micro USB B Plug  # not connected

nets:
  N1: Teensy1.pin_1, Teensy1.pin_32
  N2: Teensy1.pin_7, DG01D-E_Motor_with_Encoder3.H1
  N3: Teensy1.pin_8, DG01D-E_Motor_with_Encoder3.H2
  N4: Teensy1.pin_9, DG01D-E_Motor_with_Encoder4.H1
  N5: Teensy1.pin_10, DG01D-E_Motor_with_Encoder4.H2
  N6: Teensy1.pin_21, USBTTL5.usb, USBTTL8.usb
  N7: Teensy1.pin_25, Mod2.J1_SDA, Mod2.J2_SDA, Mod2.J4_SDA, Part1.SDA
  N8: Teensy1.pin_26, Mod2.J1_SCL, Mod2.J2_SCL, Mod2.J3_SCL, Mod2.J4_SCL, Part1.SCL
  3V3: Mod2.J1_VCC, Mod2.J4_VCC, DG01D-E_Motor_with_Encoder3.V, DG01D-E_Motor_with_Encoder4.V, Mod3.3V3, Mod3.5V, Mod3.GPIO2, Part1.+3.3V
  GND: Mod2.J1_GND, Mod2.J4_GND, DG01D-E_Motor_with_Encoder3.Gnd, DG01D-E_Motor_with_Encoder4.Gnd, Mod3.GND, Mod3.GPIO17, Mod3.GPIO18, Part1.GND, VCC2.-
  N9: DG01D-E_Motor_with_Encoder3.M-, Part1.M3B
  N10: DG01D-E_Motor_with_Encoder3.M+, Part1.M3A
  N11: DG01D-E_Motor_with_Encoder4.M-, Part1.M4B
  N12: DG01D-E_Motor_with_Encoder4.M+, Part1.M4A
  N13: RPLidarA2M4.RX, RPLidarA2M5.RX
  N14: RPLidarA2M4.TX, RPLidarA2M5.TX
  GND_2: RPLidarA2M4.GND, RPLidarA2M5.GND
  N15: RPLidarA2M4.PWM, RPLidarA2M5.PWM
  5V: RPLidarA2M4.5V, RPLidarA2M5.VCC
  N16: USBTTL6.usb, USBTTL7.usb
  N17: Part1.VMOTOR, VCC2.+

notes:
  - G (Blue): hall power negative
  - H1 (Green): hall H1 output signal, square wave
  - H2 (Yellow): hall H2 output signal, square wave
  - V (Orange): hall power positive
  - M+ (Red): motor positive pole
  - M- (Brown): motor negative pole
  USB Powerbank
  5V

custom parts:
  Teensy 4.0: The Teensy is a complete USB-based microcontoller development system, in a very small footprint, capable of implementing many types of projects. All programming is done via the USB port. No special programmer is needed, only a standard micro-USB cable and a PC or Macintosh with a USB port.
  Grove I2C hub: Seeed Grove I2C Hub
  Hobby Motor with Encoder - Metal Gear (DG01D-E): The DG01D-E is a single hobby motor with a hall speed encoder. This motor requires a voltage between 3-9V, has a gearbox ratio of 1:48 and a speed of 90RPM at 4.5V. The voltage between positive and negative is determined according to the power supply voltage of the single chip microcomputer used, generally 3.3V or 5V is used. The hall sensor can sense the North and South poles of its magnetic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
  RPLidar A2 M8 Serial to USB converter: SLAMTEC RPLidar A2 M8 Serial to USB converter
  Micro USB B Plug: Micro USB B Plug breadboard only for documetnation purposes.
  USB A Plug: USB A Plug breadboard only for documetnation purposes.
  RPLidar A2 M8: SLAMTEC RPLidar A2 M8
  Adafruit DC+Stepper FeatherWing: This is the DC Motor + Stepper FeatherWing which will let you use 2 x bi-polar stepper motors or 4 x brushed DC motorx (or 1 stepper and 2 DC motors). Using our Feather Stacking Headers or Feather Female Headers you can connect a FeatherWing on top or bottom of your Feather board and let the board take flight! The original Adafruit Motorshield Kit is one of our most beloved kits, which is why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
