# Fritzing sketch diffbot (saved by Fritzing 0.9.3b)
breadboards: 1

parts:
  Teensy1 = Teensy 4.0
  VCC1 = 4 x AAA Battery Mount
  Mod2 = Grove I2C hub
  DG01D-E_Motor_with_Encoder3 = Hobby Motor with Encoder - Metal Gear (DG01D-E) [part_number=VT-E-G25A-06-177E]
  DG01D-E_Motor_with_Encoder4 = Hobby Motor with Encoder - Metal Gear (DG01D-E) [part_number=VT-E-G25A-06-177E]
  RPLidarA2M4 = RPLidar A2 M8 Serial to USB converter
  USBTTL5 = Micro USB B Plug
  USBTTL6 = USB A Plug
  USBTTL7 = Micro USB B Plug
  USBTTL8 = USB A Plug
  Mod3 = Raspberry Pi 4B
  RPLidarA2M5 = RPLidar A2 M8
  IC2 = Grove - I2C Motor Driver V1.3 [package="DIP (Dual Inline) [THT]"]

nets:
  N1: Teensy1.pin_1, Teensy1.pin_32
  N2: Teensy1.pin_7, DG01D-E_Motor_with_Encoder3.H1
  N3: Teensy1.pin_8, DG01D-E_Motor_with_Encoder3.H2
  N4: Teensy1.pin_9, DG01D-E_Motor_with_Encoder4.H1
  N5: Teensy1.pin_10, DG01D-E_Motor_with_Encoder4.H2
  N6: Teensy1.pin_21, USBTTL5.usb, USBTTL8.usb
  N7: VCC1.-, IC2.GND#12
  N8: VCC1.+, IC2.VS
  GND: Mod2.J1_SCL, Mod2.J1_GND, Mod2.J2_SCL, Mod2.J4_SCL, Mod2.J4_GND, DG01D-E_Motor_with_Encoder3.Gnd, DG01D-E_Motor_with_Encoder4.Gnd, Mod3.GPIO3, Mod3.GND, IC2.GND#8, IC2.SCL
  5V: Mod2.J1_SDA, Mod2.J1_VCC, Mod2.J4_SDA, Mod2.J4_VCC, DG01D-E_Motor_with_Encoder3.V, DG01D-E_Motor_with_Encoder4.V, Mod3.5V, Mod3.GPIO2, IC2.VCC, IC2.SDA
  N9: DG01D-E_Motor_with_Encoder3.M-, IC2.M1-
  N10: DG01D-E_Motor_with_Encoder3.M+, IC2.M1+
  N11: DG01D-E_Motor_with_Encoder4.M-, IC2.M2-
  N12: DG01D-E_Motor_with_Encoder4.M+, IC2.M2+
  N13: RPLidarA2M4.RX, RPLidarA2M5.RX
  N14: RPLidarA2M4.TX, RPLidarA2M5.TX
  GND_2: RPLidarA2M4.GND, RPLidarA2M5.GND
  N15: RPLidarA2M4.PWM, RPLidarA2M5.PWM
  5V_2: RPLidarA2M4.5V, RPLidarA2M5.VCC
  N16: USBTTL6.usb, USBTTL7.usb

notes:
  - G (Blue): hall power negative
  - H1 (Green): hall H1 output signal, square wave
  - H2 (Yellow): hall H2 output signal, square wave
  - V (Orange): hall power positive
  - M+ (Red): motor positive pole
  - M- (Brown): motor negative pole

custom parts:
  Teensy 4.0: The Teensy is a complete USB-based microcontoller development system, in a very small footprint, capable of implementing many types of projects. All programming is done via the USB port. No special programmer is needed, only a standard micro-USB cable and a PC or Macintosh with a USB port.
  Grove I2C hub: Seeed Grove I2C Hub
  Hobby Motor with Encoder - Metal Gear (DG01D-E): The DG01D-E is a single hobby motor with a hall speed encoder. This motor requires a voltage between 3-9V, has a gearbox ratio of 1:48 and a speed of 90RPM at 4.5V. The voltage between positive and negative is determined according to the power supply voltage of the single chip microcomputer used, generally 3.3V or 5V is used. The hall sensor can sense the North and South poles of its magnetic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
  RPLidar A2 M8 Serial to USB converter: SLAMTEC RPLidar A2 M8 Serial to USB converter
  Micro USB B Plug: Micro USB B Plug breadboard only for documetnation purposes.
  USB A Plug: USB A Plug breadboard only for documetnation purposes.
  RPLidar A2 M8: SLAMTEC RPLidar A2 M8
  Grove - I2C Motor Driver V1.3: The Grove - I2C Motor Driver V1.3 (latest version) can directly control Stepper Motor or DC Motor. Its heart is a dual channel H-bridge driver chip（L298N）that can handle current up to 2A per channel, controlled by an Atmel ATmega8L which handles the I2C communication with platforms such as Arduino. Both motors can be driven simultaneously while set to a different speed and direction. It can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
